// Logisim project pipeline.circ as structural Verilog
module FetchUnit (
  input  [7:0] instrORimm,
  input  clk,
  input  reset,
  input  delay,
  input  insertNOPE,
  output ready,
  output [7:0] PipelineRegisters,
  output [7:0] nextStage,
  output incPC
);

  wire and_1_out, nor_1_out, not_1_out, not_2_out, or_1_out;
  wire [1:0] counter_1_q;
  wire [7:0] multiplexer_1_out, register_1_q;

  // NoConnect on instrORimm[0]
  // NoConnect on instrORimm[1]
  // NoConnect on instrORimm[2]
  // NoConnect on instrORimm[3]
  // NoConnect on instrORimm[4]
  // NoConnect on instrORimm[5]
  Register register_1 (.D(instrORimm), .en(not_1_out), .clk(clk), .Q(register_1_q), .clr(reset));
  not not_1 (not_1_out, delay);
  not not_2 (not_2_out, insertNOPE);
  or or_1 (or_1_out, instrORimm[6], instrORimm[7]);
  nor nor_1 (nor_1_out, counter_1_q[0], counter_1_q[1]);
  and and_1 (and_1_out, nor_1_out, or_1_out);
  Multiplexer #(.width(8)) multiplexer_1 (
    .in0({8{1'b0}}), .in1(register_1_q), .out(multiplexer_1_out), .sel(not_2_out));
  Counter #(.max('h3), .ongoal("stay"), .width(2)) counter_1 (
    .load(and_1_out), .D(instrORimm[7:6]), .count(1'b1), .Q(counter_1_q), .up(1'b0), .clk(clk), .clr(reset));  // open: carry
  Demultiplexer #(.width(8)) demultiplexer_1 (
    .out0(PipelineRegisters), .out1(nextStage), .in(multiplexer_1_out));  // open: sel
  and and_2 (ready, ~counter_1_q[0], ~counter_1_q[1]);  // AND_Gate
endmodule
